# Fritzing sketch RRFDisplay_RPI (saved by Fritzing 0.9.3b)

parts:
  Raspberry_Pi_1 = Raspberry Pi 3 [part_number=RPI-3-V1.2]
  Squix1 = OLED 0.96" 128x64 I2C SSD1306

nets:
  3V3: Raspberry_Pi_1.3v3, Squix1.VCC
  N1: Raspberry_Pi_1.GPIO2, Squix1.SCA
  N2: Raspberry_Pi_1.GPIO3, Squix1.SCL
  GND: Raspberry_Pi_1.GND, Squix1.GND
